# Fritzing sketch pj1 (saved by Fritzing 1.0.4)
circuit board: 9.94325cm x 6.44265cm

parts:
  Driver1 = 28BYJ-48 Driver Module [part_number=ULN2003 package=THT]
  SM1 = 28BYJ-48 Stepper Motor [part_number=28BYJ-48]
  OLED1 = SSD1306 0.96in 128x64 I2C Monochrome OLED Display
  U1 = LuaNode32 / ESP32
  DS1307 = Adafruit DS1307 RTC Breakout [part_number="Adafruit #264"]
  S2 = Pushbutton [package="[THT]"]

nets:
  N1: Driver1.IN1, U1.D26
  N2: Driver1.IN2, U1.D25
  N3: Driver1.IN3, U1.D33
  N4: Driver1.IN4, U1.D32
  GND: Driver1.GND, OLED1.GND, U1.GND, DS1307.GND, S2.Pin_1, S2.Pin_2
  VCC: Driver1.Vmotor, OLED1.VCC, U1.Vin, DS1307.VCC
  N5: Driver1.blue-pin, SM1.blue-pin
  N6: Driver1.pink-pin, SM1.pink-pin
  N7: Driver1.yellow-pin, SM1.yellow-pin
  N8: Driver1.orange-pin, SM1.orange-pin
  N9: Driver1.red-pin, SM1.red-pin
  N10: OLED1.SCL, U1.D22, DS1307.SCL
  N11: OLED1.SDA, U1.D21, DS1307.SDA
  N12: U1.D19, S2.Pin_3, S2.Pin_4

custom parts:
  28BYJ-48 Driver Module: ULN2003 Driver Module for the 28BYJ-48 Unipolar Stepper Motor LED A - Blue wire - Bottom coil left LED B - Pink wire - Top coil left LED C - Yellow wire - Bottom coil right LED D - Orange wire - Top coil right Common rail - red Connector pins: blue - pink - yellow - orange - red Control pins - IN1 to IN4 Power pins - GND & Vmotor (5-12V) On/Off jumper (if removed, power to motor is cut).
  28BYJ-48 Stepper Motor: Unipolar Stepper Motor 28BYJ-48 Top coil - pink & orange Bottom coil - blue & yellow Common rail - red Connector pins: blue - pink - yellow - orange - red
  LuaNode32 / ESP32: ESP32 based LuaNode32
  Adafruit DS1307 RTC Breakout: This is a great battery-backed real time clock (RTC) that allows your microcontroller project to keep track of time even if it is reprogrammed, or if the power is lost. Perfect for datalogging, clock-building, time stamping, timers and alarms, etc. The DS1307 is the most popular RTC - but it requires 5V power to work (although we've used it with 5V power and 3.3V logic successfully) PCB &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
